# Fritzing sketch MKR_WiFi_1010 (saved by Fritzing 0.9.3b)
breadboards: 1

parts:
  RTC1 = RTC-8564NB [package="Module(DIP 8P)"]
  パーツ1 = Adafruit MicroSD card breakout board [part_number="Adafruit #254"]
  Mod1 = Arduino MKR Wifi 1010

nets:
  GND: RTC1.GND, パーツ1.GND, Mod1.GND
  N1: RTC1.SDA, Mod1.D11/SDA
  N2: RTC1.SCL, Mod1.D12/SCL
  +3V3: RTC1.VDD, パーツ1.+3V3, Mod1.+3V3
  N3: パーツ1.CLK, Mod1.D9/SCK
  N4: パーツ1.DO, Mod1.D10/MISO
  N5: パーツ1.DI, Mod1.D8/MOSI
  N6: パーツ1.CS, Mod1.~D4

custom parts:
  RTC-8564NB: Real Time Clock Module and I2C-BUS interface method. This product is a module of the SON 8-pin DIP package. Supply voltage 1.8-5.5V original version by KimuShige
  Adafruit MicroSD card breakout board: Not just a simple breakout board, this microSD adapter goes the extra mile - designed for ease of use. Onboard 5v->3v regulator provides 150mA for power-hungry cards 3v level shifting means you can use this with ease on either 3v or 5v systems Uses a proper level shifting chip, not resistors: less problems, and faster read/write access Use 3 or 4 digital pins to read and write 2Gb+ of storage!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
  Arduino MKR Wifi 1010: Arduino MKR Wifi 1010, SAMD21 Cortex-M0+ 32bit Low Power ARM MCU,Flash Memory 256 KB, SRAM 32KB, 48mhz clock, Ublok Wifi interface.
