# Fritzing sketch Mega (saved by Fritzing 0.9.3b)
breadboards: 1

parts:
  パーツ1 = Arduino Mega 2560 (Rev3)
  パーツ3 = Arduino Ethernet Shield (Rev3)
  RTC1 = RTC-8564NB [package="Module(DIP 8P)"]
  パーツ4 = FTDI Basic Programmer

nets:
  N1: パーツ1.A0, パーツ3.A0
  N2: パーツ1.A1, パーツ3.A1
  N3: パーツ1.A2, パーツ3.A2
  N4: パーツ1.A3, パーツ3.A3
  N5: パーツ1.A4, パーツ1.SDA, パーツ3.A4/SDA, RTC1.SDA
  N6: パーツ1.A5, パーツ1.SCL, パーツ3.A5/SCL, RTC1.SCL
  N7: パーツ1.AREF, パーツ3.AREF
  GND: パーツ1.GND, パーツ3.GND, RTC1.GND, パーツ4.GND
  N8: パーツ1.D13_PWM, パーツ3.SPI/D13
  N9: パーツ1.D12_PWM, パーツ4.TXO
  N10: パーツ1.D11_PWM, パーツ4.RXI
  N11: パーツ1.D10_PWM, パーツ3.ETH_CS
  N12: パーツ1.D9_PWM, パーツ3.PWM_D9
  N13: パーツ1.D8_PWM, パーツ3.D8
  N14: パーツ1.IOREF#254, パーツ3.N/A
  N15: パーツ1.IOREF#255, パーツ3.IOREF
  N16: パーツ1.RESET, パーツ3.RESET
  3V3: パーツ1.3V3, パーツ3.3V3
  5V: パーツ1.5V, パーツ3.5V, RTC1.VDD
  VIN: パーツ1.VIN, パーツ3.VIN
  N17: パーツ1.D0_RX0, パーツ3.RX/D0
  N18: パーツ1.D1_TX0, パーツ3.TX/D1
  N19: パーツ1.D2_PWM, パーツ3.D2
  N20: パーツ1.D3_PWM, パーツ3.PWM_D3
  N21: パーツ1.D4_PWM, パーツ3.SDCS
  N22: パーツ1.D5_PWM, パーツ3.PWM_D5
  N23: パーツ1.D6_PWM, パーツ3.PWM_D6
  N24: パーツ1.D7_PWM, パーツ3.D7

custom parts:
  RTC-8564NB: Real Time Clock Module and I2C-BUS interface method. This product is a module of the SON 8-pin DIP package. Supply voltage 1.8-5.5V original version by KimuShige
