# Fritzing sketch esp32 (saved by Fritzing 0.9.3b)
breadboards: 1

parts:
  RTC1 = RTC-8564NB [package="Module(DIP 8P)"]
  パーツ1 = Adafruit MicroSD card breakout board [part_number="Adafruit #254"]
  ESP1 = SWITCH SCIENCE ESPr Developer 32

nets:
  GND: RTC1.GND, パーツ1.GND, ESP1.gnd
  N1: RTC1.SDA, ESP1.io21
  N2: RTC1.SCL, ESP1.io22
  VDD: RTC1.VDD, パーツ1.+3V3, ESP1.3v3
  N3: パーツ1.CLK, ESP1.io18
  N4: パーツ1.DO, ESP1.io19
  N5: パーツ1.DI, ESP1.io23
  N6: パーツ1.CS, ESP1.io4

custom parts:
  RTC-8564NB: Real Time Clock Module and I2C-BUS interface method. This product is a module of the SON 8-pin DIP package. Supply voltage 1.8-5.5V original version by KimuShige
  Adafruit MicroSD card breakout board: Not just a simple breakout board, this microSD adapter goes the extra mile - designed for ease of use. Onboard 5v->3v regulator provides 150mA for power-hungry cards 3v level shifting means you can use this with ease on either 3v or 5v systems Uses a proper level shifting chip, not resistors: less problems, and faster read/write access Use 3 or 4 digital pins to read and write 2Gb+ of storage!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
